# Fritzing sketch dc_meter (saved by Fritzing 0.9.3b)
breadboards: 1

parts:
  ACS709_Stromsensor_Breakout_Board_-75_to_+75A1 = ACS709 Stromsensor Breakout Board -75 to +75A
  Componente1 = Arduino Yun
  R1 = Resistor [tolerance=±5% resistance=10k package="1206 [SMD]"]
  R2 = Resistor [tolerance=±5% resistance=100k package="0805 [SMD]"]
  J1 = Screw terminal - 2 pins [package=THT]
  J2 = Screw terminal - 2 pins [package=THT]
  J3 = Screw terminal - 2 pins [package=THT]
  ASA01A18-LS1 = ASA01A18-LS

nets:
  N1: ACS709_Stromsensor_Breakout_Board_-75_to_+75A1.Messpunkt_+IN, R2.Pin_1, J2.pin1, J2.pin2, ASA01A18-LS1.Vin_+
  N2: ACS709_Stromsensor_Breakout_Board_-75_to_+75A1.Messpunkt_+OUT, J1.pin1, J1.pin2
  N3: ACS709_Stromsensor_Breakout_Board_-75_to_+75A1.VIOUT, Componente1.A0
  VCC: ACS709_Stromsensor_Breakout_Board_-75_to_+75A1.VCC, Componente1.VIN, ASA01A18-LS1.Vout_+
  GND: ACS709_Stromsensor_Breakout_Board_-75_to_+75A1.GND, Componente1.GND, R1.Pin_0, J3.pin1, J3.pin2, ASA01A18-LS1.Vin_-, ASA01A18-LS1.GND
  N4: Componente1.A1, R1.Pin_1, R2.Pin_0

notes:
  orange= BATT in
  purple = BATT out
  black = GND
  DC power smart meter
  with voltage and current sensors

custom parts:
  ACS709 Stromsensor Breakout Board -75 to +75A: Stromsensor Bereich -75A bis +75A
  ASA01A18-LS: Artesyn ASTEC ASA01A18-LS DC-DC Converter 9-36V to 5V , 1 amp
